# Fritzing sketch kiln_controller (saved by Fritzing 0.9.2b)
circuit board: 8.46667cm x 5.64444cm

parts:
  Part1 = Adafruit Perma-Proto HAT [part_number="Adafruit #2314 and #2310"]
  Part3 = Adafruit MAX31856 Thermocouple Amp [part_number="Adafruit #3263"]
  Part4 = Adafruit I2C+SPI LCD Backpack [part_number="Adafruit #292"]
  JP4 = FTDI_BASIC [package=ftdi_basic]
  JP6 = FTDI_BASIC [package=ftdi_basic]
  IC2 = MCP3008 8-channel 10-bit ADC [part_number=MCP3008]
  Relay1 = 941 Series Relay [package=THT]
  Relay1_1 = 941 Series Relay [package=THT]  # not connected
  Relay1_2 = 941 Series Relay [package=THT]  # not connected
  Relay1_3 = 941 Series Relay [package=THT]  # not connected
  Relay2_3 = 941 Series Relay [package=THT]  # not connected
  Relay2_2 = 941 Series Relay [package=THT]  # not connected
  Relay2 = 941 Series Relay [package=THT]
  Relay2_1 = 941 Series Relay [package=THT]  # not connected
  Relay3_2 = 941 Series Relay [package=THT]  # not connected
  Relay3_1 = 941 Series Relay [package=THT]  # not connected
  Relay3 = 941 Series Relay [package=THT]
  Relay3_3 = 941 Series Relay [package=THT]  # not connected
  Part5 = Adafruit MAX31856 Thermocouple Amp [part_number="Adafruit #3263"]
  JP7 = FTDI_BASIC [package=ftdi_basic]
  JP8 = FTDI_BASIC [package=ftdi_basic]

nets:
  N1: Part1.GPIO22, Part1.N$60
  N2: Part1.GPIO23, Part1.N$57
  N3: Part1.GPIO24, Part1.N$55
  N4: Part1.SPI_MISO, Part1.N$51#321
  N5: Part1.SPI_SCLK, Part1.N$49#311
  N6: Part1.SPI_CE1, Part1.N$10#202
  N7: Part1.5.0V, Part4.VCC
  N8: Part1.SDA, Part4.DATA
  N9: Part1.SCL, Part4.CLOCK
  GND: Part1.GND, Part1.N$14#221, Part1.N$50#316, Part4.GND
  N10: Part1.3.3V, Part1.N$48#306
  N11: Part1.N$1#156, Relay1.connector0, Relay2.connector0, Relay3.connector0
  N12: Part1.N$4, Relay3.connector15
  N13: Part1.N$6, Relay1.connector15
  N14: Part1.N$7, Relay2.connector15
  N15: Part1.N$10#205, JP6.1
  N16: Part1.N$11#208, Part1.N$52#328
  N17: Part1.N$11#210, JP6.2
  N18: Part1.N$12#213, Part1.N$51#323
  N19: Part1.N$12#215, JP6.3
  N20: Part1.N$13#218, Part1.N$49#313
  N21: Part1.N$13#220, JP6.4
  N22: Part1.N$14#225, JP6.5
  N23: Part1.N$15#228, Part1.N$48#308
  N24: Part1.N$15#230, JP6.6
  N25: Part1.N$48#307, JP4.6
  N26: Part1.N$49#312, JP4.4
  N27: Part1.N$50#317, JP4.5
  N28: Part1.N$51#322, JP4.3
  N29: Part1.N$52#327, JP4.2
  N30: Part1.N$54, JP4.1
  N31: Part3.!CS, JP7.1
  N32: Part3.SDI, JP7.2
  N33: Part3.SDO, JP7.3
  N34: Part3.SCK, JP7.4
  N35: Part3.GND, JP7.5
  N36: Part3.3.3V, JP7.6
  N37: IC2.out_7, IC2.out_5, IC2.out_3, IC2.out_1
  N38: Relay1.connector3, Relay2.connector3, Relay3.connector3
  N39: Relay1.connector12, Relay2.connector12, Relay3.connector12
  N40: Part5.!CS, JP8.1
  N41: Part5.SDI, JP8.2
  N42: Part5.SDO, JP8.3
  N43: Part5.SCK, JP8.4
  N44: Part5.GND, JP8.5
  N45: Part5.3.3V, JP8.6

notes:
  20x4 Char LCD i2c backpack
  Kiln TC
  -
  12V
  +
  kilnsitter
  as a sensor
  L1 L2
  240VAC
  Top Middle Bottom
  Elements
  Room Air TC
  -in out-
  12v 5V
  +in out+
  3 - Relays
  Deltrol
  20852-81

custom parts:
  Adafruit Perma-Proto HAT: To kick off the Adafruit HAT party, we have this Perma-Proto inspired plug in daughter board. It has a grid of 0.1" prototyping soldering holes for attaching chips, resistors, LED, potentiometers and more. The holes are connected underneath with traces to mimic the solderless breadboards you're familiar. There's also long power strips for +3V, +5V and Ground connections to the Pi. Near the top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
  Adafruit MAX31856 Thermocouple Amp: Thermocouples are very sensitive, requiring a good amplifier with a cold-compensation reference, as well as calculations to handle any non-linearities. For a long time we've suggested our MAX31855K breakout, which works great but is only for K-type thermocouples. Now we're happy to offer a great new thermocouple amplifier/converter that can handle just about any type of thermocouple, and even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
  Adafruit I2C+SPI LCD Backpack: LCD backpacks reduce the number of pins needed to connect to an LCD. LCDs are a fun and easy way to have your microcontroller project talk back to you. Character LCDs are common, and easy to get, available in tons of colors and sizes. We've written tutorials on using character LCDs with an Arduino (or similar microcontroller) but find that the number of pins necessary to control the LCD can be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
  FTDI_BASIC: FTDI Basic header with labels
  941 Series Relay: DPDT Dual in-line relay
  941 Series Relay: DPDT Dual in-line relay
  941 Series Relay: DPDT Dual in-line relay
  941 Series Relay: DPDT Dual in-line relay
